# Fritzing sketch fzz chart (saved by Fritzing 0.9.3b)
breadboards: 1

parts:
  Raspberry_Pi_1 = Raspberry Pi 3 [part_number=RPI-3-V1.2]
  R1 = PHOTOCELL [package=photocell-kit]
  part = Resistor [tolerance=±5% resistance=220 package="2512 [SMD]"]
  LED1 = smd LED [color="Red (633nm)" package="1206 [SMD]"]
  R3 = PHOTOCELL [package=photocell]

nets:
  N1: Raspberry_Pi_1.3v3, R1.P$1, LED1.anode, R3.P$1
  N2: Raspberry_Pi_1.GPIO2, R1.P$2
  N3: Raspberry_Pi_1.GPIO3, R3.P$2
  N4: Raspberry_Pi_1.GND, part.Pin_1
  N5: part.Pin_0, LED1.cathode
